# Fritzing sketch automatic_servo_schematics (saved by Fritzing 0.9.3b)

parts:
  Part1 = Zeta LCD keypad shield for Arduino
  Part2 = Arduino Uno (Rev3)  # not connected
  J1 = Basic Servo
  J2 = Piezo Speaker
  VCC1 = Battery block 9V  # not connected

nets:
  +5V: Part1.+5V, J1.vcc
  GND: Part1.GND, J1.gnd, J2.pin1
  N1: Part1.D2, J1.pulse
  N2: Part1.D3, J2.pin2

custom parts:
  Zeta LCD keypad shield for Arduino: The LCD shield for Arduino
